# Fritzing sketch ESP32-ELM327-BT (saved by Fritzing 0.9.3b)
circuit board: 9.61871cm x 6.76387cm

parts:
  ES1 = ESP32 DEVKIT 38 pins
  OL1 = OLED 0.96" 128x64 I2C SSD1306
  C1 = Electrolytic Capacitor [capacitance=470µF package="100 mil [THT, electrolytic]"]
  buz1 = Piezo Buzzer

nets:
  3V3: ES1.3V3, OL1.VCC, C1.+
  N1: ES1.GND#64, OL1.GND, C1.-
  N2: ES1.IO22, OL1.SCL
  N3: ES1.IO21, OL1.SCA
  N4: ES1.GND#70, buz1.pin_2
  N5: ES1.IO16, buz1.pin_1

custom parts:
  ESP32 DEVKIT 38 pins: github.com/AlexVakhnin
  Piezo Buzzer: Part from https://www.nutsvolts.com/magazine/article/november2012_SmileysWorkshop. Breadboard and icon images modified to be 0.3" in spacing and be more similar to the actual physical part.
